# Fritzing sketch Schema Collegamenti Hardware (saved by Fritzing 0.9.3b)
breadboards: 1

parts:
  MH-ET_LIVE_ESP32_DEVKIT1 = MH-ET LIVE ESP32 DEVKIT 38 pins
  S1 = Pushbutton [package="[THT]"]
  S2 = Pushbutton [package="[THT]"]
  U2 = Module 4 Relais 5V [package="Module 4 Relais 5V"]
  R1 = Resistor [tolerance=±5% resistance=220 package=THT]
  LED1 = LED - 5mm [color="Red (633nm)" package="5 mm [THT]"]
  Mod1 = KY-015 Temperature & Humidity Sensor Module [package="Breakout board"]
  LCM1602_IIC1 = LCM1602 IIC [part_number="LCM1602 IIC" chip_label="LCM1602 IIC" package="DIP (Dual Inline) [THT]"]
  LCD1 = LCD screen

nets:
  N1: MH-ET_LIVE_ESP32_DEVKIT1.IO32, U2.IN1
  N2: MH-ET_LIVE_ESP32_DEVKIT1.IO33, Mod1.Vin
  N3: MH-ET_LIVE_ESP32_DEVKIT1.IO25, S2.Pin_3, S2.Pin_4
  N4: MH-ET_LIVE_ESP32_DEVKIT1.IO26, S1.Pin_3, S1.Pin_4
  GND: MH-ET_LIVE_ESP32_DEVKIT1.GND#58, S1.Pin_1, S1.Pin_2, S2.Pin_1, S2.Pin_2, U2.GND, LED1.anode, Mod1.-, LCM1602_IIC1.GND
  VCC: MH-ET_LIVE_ESP32_DEVKIT1.5V, U2.VCC, U2.K1-NO, Mod1.S, LCM1602_IIC1.VCC
  N5: MH-ET_LIVE_ESP32_DEVKIT1.IO22, LCM1602_IIC1.SCL
  N6: MH-ET_LIVE_ESP32_DEVKIT1.IO21, LCM1602_IIC1.SDA
  N7: U2.K1-NF, R1.Pin_0
  N8: R1.Pin_1, LED1.cathode
  VSS: LCM1602_IIC1.VSS, LCD1.VSS
  VDD: LCM1602_IIC1.VDD, LCD1.VDD
  N9: LCM1602_IIC1.V0, LCD1.V0
  N10: LCM1602_IIC1.RS, LCD1.RS
  N11: LCM1602_IIC1.RW, LCD1.R/W
  N12: LCM1602_IIC1.E, LCD1.E
  N13: LCM1602_IIC1.D0, LCD1.DB0
  N14: LCM1602_IIC1.D1, LCD1.DB1
  N15: LCM1602_IIC1.D2, LCD1.DB2
  N16: LCM1602_IIC1.D3, LCD1.DB3
  N17: LCM1602_IIC1.D4, LCD1.DB4
  N18: LCM1602_IIC1.D5, LCD1.DB5
  N19: LCM1602_IIC1.D6, LCD1.DB6
  N20: LCM1602_IIC1.D7, LCD1.DB7
  N21: LCM1602_IIC1.A, LCD1.LED+
  N22: LCM1602_IIC1.K, LCD1.LED-
  N23: LCM1602_IIC1.LED_A, LCM1602_IIC1.LED_B

custom parts:
  MH-ET LIVE ESP32 DEVKIT 38 pins: http://mh.nodebb.com/topic/2/mh-et-live-esp32-devkit
  Module 4 Relais 5V: Module 4 Relais 5V 4x SPD-06VDC-SD-C
  KY-015 Temperature & Humidity Sensor Module: KY-015 temperature and humidity sensor module, provides a low-latency serial interface to measure humidity and temperature.
  LCM1602 IIC: I2C-Module to use a 1602 or 2004 LCD on with the wire.h libory Serial LCD Modul
